// Digital circuit 4-by-3-memory-first-try.dig as structural Verilog
module _4_by_3_memory_first_try (
  input  D_3,
  input  clk,
  input  in_4,
  input  in_5,
  input  in_6,
  input  in_7,
  input  D_2,
  input  D_1,
  input  D_0,
  input  [7:0] in_14,
  input  [2:0] in_16,
  output Q_3,
  output Q_2,
  output Q_1,
  output Q_0,
  output out_15
);

  wire and_1_out, and_2_out, and_3_out, d_ff_1_q, d_ff_2_q, d_ff_3_q, d_ff_4_q, d_ff_5_q, d_ff_6_q, d_ff_7_q,
       d_ff_8_q, d_ff_9_q, d_ff_10_q, d_ff_11_q, d_ff_12_q, decoder_1_out_0, decoder_1_out_1, decoder_1_out_2;

  Decoder #(.Selector_Bits(2)) decoder_1 (
    .sel({in_6, in_7}), .out_0(decoder_1_out_0), .out_1(decoder_1_out_1), .out_2(decoder_1_out_2));  // open: out_3
  and and_1 (and_1_out, decoder_1_out_0, clk);
  and and_2 (and_2_out, decoder_1_out_1, clk);
  and and_3 (and_3_out, decoder_1_out_2, clk);
  BitSelector #(.Selector_Bits(3)) bitselector_1 (.in(in_14), .sel(in_16), .out(out_15));
  D_FF d_ff_1 (.D(D_3), .C(and_1_out), .Q(d_ff_1_q));  // open: nQ
  D_FF d_ff_2 (.D(D_3), .C(and_2_out), .Q(d_ff_2_q));  // open: nQ
  D_FF d_ff_3 (.D(D_3), .C(and_3_out), .Q(d_ff_3_q));  // open: nQ
  Multiplexer #(.Selector_Bits(2)) multiplexer_1 (
    .sel({in_4, in_5}), .in_0(d_ff_1_q), .in_1(d_ff_2_q), .in_2(d_ff_3_q), .in_3(1'b0), .out(Q_3));
  D_FF d_ff_4 (.D(D_2), .C(and_3_out), .Q(d_ff_4_q));  // open: nQ
  D_FF d_ff_5 (.D(D_2), .C(and_1_out), .Q(d_ff_5_q));  // open: nQ
  D_FF d_ff_6 (.D(D_2), .C(and_2_out), .Q(d_ff_6_q));  // open: nQ
  Multiplexer #(.Selector_Bits(2)) multiplexer_2 (
    .sel({in_4, in_5}), .in_0(d_ff_5_q), .in_1(d_ff_6_q), .in_2(d_ff_4_q), .in_3(1'b0), .out(Q_2));
  D_FF d_ff_7 (.D(D_1), .C(and_1_out), .Q(d_ff_7_q));  // open: nQ
  D_FF d_ff_8 (.D(D_1), .C(and_2_out), .Q(d_ff_8_q));  // open: nQ
  D_FF d_ff_9 (.D(D_1), .C(and_3_out), .Q(d_ff_9_q));  // open: nQ
  Multiplexer #(.Selector_Bits(2)) multiplexer_3 (
    .sel({in_4, in_5}), .in_0(d_ff_7_q), .in_1(d_ff_8_q), .in_2(d_ff_9_q), .in_3(1'b0), .out(Q_1));
  D_FF d_ff_10 (.D(D_0), .C(and_3_out), .Q(d_ff_10_q));  // open: nQ
  D_FF d_ff_11 (.D(D_0), .C(and_1_out), .Q(d_ff_11_q));  // open: nQ
  D_FF d_ff_12 (.D(D_0), .C(and_2_out), .Q(d_ff_12_q));  // open: nQ
  Multiplexer #(.Selector_Bits(2)) multiplexer_4 (
    .sel({in_4, in_5}), .in_0(d_ff_11_q), .in_1(d_ff_12_q), .in_2(d_ff_10_q), .in_3(1'b0), .out(Q_0));

  // Notes on the sheet:
  //   in_16: default 7
  //   write-addr
  //   read-addr
  //   Nibble at address 0
  //   Nibble at address 1
  //   Nibble at address 2
  //   Address Space: 3
  //   Addressability: 4-bit
endmodule
