// Digital circuit part2 circuit.dig as structural Verilog
module part2_circuit (
  input  [31:0] operand_0,
  input  [31:0] operand_1,
  input  [3:0] operation,
  output [31:0] result
);

  wire notconnected_2_out;
  wire [31:0] add_1_s, and_1_out, not_1_out, notconnected_1_out, or_1_out, sub_1_s, sub_2_s, xor_1_out;

  assign not_1_out = ~operand_1;  // Not not_1, 32 bits wide
  assign or_1_out = operand_1 | operand_0;  // Or or_1, 32 bits wide
  // NotConnected on notconnected_1_out
  Add #(.Bits(32)) add_1 (.a(operand_0), .b(operand_1), .c_i(notconnected_2_out), .s(add_1_s));  // open: c_o
  // NotConnected on notconnected_2_out
  Multiplexer #(.Selector_Bits(4), .Bits(32)) multiplexer_1 (
    .sel(operation), .in_0(and_1_out), .in_1(xor_1_out), .in_2(sub_2_s), .in_3(sub_1_s), .in_4(add_1_s),
    .in_5(notconnected_1_out), .in_6(notconnected_1_out), .in_7(notconnected_1_out),
    .in_8(notconnected_1_out), .in_9(notconnected_1_out), .in_10(notconnected_1_out),
    .in_11(notconnected_1_out), .in_12(or_1_out), .in_13(operand_1), .in_14(notconnected_1_out),
    .in_15(not_1_out), .out(result));
  Sub #(.Bits(32)) sub_1 (.a(operand_1), .b(operand_0), .c_i(notconnected_2_out), .s(sub_1_s));  // open: c_o
  Sub #(.Bits(32)) sub_2 (.a(operand_0), .b(operand_1), .c_i(notconnected_2_out), .s(sub_2_s));  // open: c_o
  assign xor_1_out = operand_0 ^ operand_1;  // XOr xor_1, 32 bits wide
  assign and_1_out = operand_0 & operand_1;  // And and_1, 32 bits wide
endmodule
