// Digital circuit HW1 Circuit.dig as structural Verilog
module HW1_Circuit (
  input  A,
  input  B,
  output A_XOR_B
);

  wire nfet_1_d, nfet_2_d, pfet_1_s, pfet_2_d, pfet_6_d;

  PFET pfet_1 (.G(A), .S(pfet_1_s), .D(1'b0));
  NFET nfet_1 (.G(A), .D(nfet_1_d), .S(1'b0));
  PFET pfet_2 (.G(A), .S(1'b1), .D(pfet_2_d));
  PFET pfet_3 (.G(nfet_1_d), .S(pfet_2_d), .D(A_XOR_B));
  NFET nfet_2 (.G(B), .D(nfet_2_d), .S(A));
  PFET pfet_4 (.G(B), .S(pfet_2_d), .D(1'b1));
  PFET pfet_5 (.G(pfet_6_d), .S(pfet_1_s), .D(A_XOR_B));
  NFET nfet_3 (.G(B), .D(1'b0), .S(nfet_1_d));
  PFET pfet_6 (.G(B), .S(1'b0), .D(pfet_6_d));
  NFET nfet_4 (.G(nfet_2_d), .D(A_XOR_B), .S(nfet_1_d));
endmodule
