// Digital circuit HW2 Circuit.dig as structural Verilog
module HW2_Circuit (
  input  [7:0] BCD_Input_1,
  input  [7:0] BCD_Input_2,
  output [11:0] BCD_Sum
);

  wire add_3_c_o, add_4_c_o, and_1_out, and_2_out, and_3_out, and_4_out;
  wire [2:2] or_2_out;
  wire [3:0] add_3_s, add_4_s;

  or or_1 (BCD_Sum[8], and_2_out, add_3_c_o, and_1_out);
  or or_2 (or_2_out[2], and_4_out, add_4_c_o, and_3_out);
  and and_1 (and_1_out, add_3_s[2], add_3_s[3]);
  and and_2 (and_2_out, add_3_s[1], add_3_s[3]);
  Add #(.Bits(4)) add_1 (.a(add_3_s), .b({1'b0, {2{BCD_Sum[8]}}, 1'b0}), .c_i(1'b0), .s(BCD_Sum[7:4]));  // open: c_o
  and and_3 (and_3_out, add_4_s[2], add_4_s[3]);
  and and_4 (and_4_out, add_4_s[1], add_4_s[3]);
  Add #(.Bits(4)) add_2 (.a(add_4_s), .b({1'b0, {2{or_2_out[2]}}, 1'b0}), .c_i(1'b0), .s(BCD_Sum[3:0]));  // open: c_o
  Add #(.Bits(4)) add_3 (.a(BCD_Input_2[7:4]), .b(BCD_Input_1[7:4]), .c_i(or_2_out[2]), .s(add_3_s), .c_o(add_3_c_o));
  Add #(.Bits(4)) add_4 (.a(BCD_Input_2[3:0]), .b(BCD_Input_1[3:0]), .c_i(1'b0), .s(add_4_s), .c_o(add_4_c_o));

  assign BCD_Sum[11:9] = 3'b000;
endmodule
