// Digital circuit HW3.dig as structural Verilog
module HW3 (
  input  [5:0] Write_Key,
  input  [7:0] Write_Value,
  input  [5:0] Read_Key,
  input  clk,
  output [7:0] Read_Value
);

  wire and_1_out, and_2_out, and_3_out, and_4_out, and_5_out, and_6_out, and_7_out, and_8_out, and_9_out,
       and_10_out, and_11_out, and_12_out, and_13_out, and_14_out, and_15_out, and_16_out, and_17_out,
       and_18_out, and_19_out, and_20_out, and_21_out, and_22_out, and_23_out, and_24_out, and_25_out,
       and_26_out, and_27_out, and_28_out, and_29_out, and_30_out, and_31_out, and_32_out, and_33_out,
       and_34_out, and_35_out, and_36_out, and_37_out, and_38_out, and_39_out, and_40_out, and_41_out,
       and_42_out, and_43_out, and_44_out, and_45_out, and_46_out, and_47_out, and_48_out, and_49_out,
       and_50_out, and_51_out, and_52_out, and_53_out, and_54_out, d_ff_1_q, decoder_1_out_0,
       decoder_1_out_1, decoder_1_out_2, decoder_1_out_3, decoder_1_out_4, decoder_1_out_5, decoder_1_out_6,
       decoder_1_out_7, decoder_2_out_0, decoder_2_out_1, decoder_2_out_2, decoder_2_out_3, decoder_2_out_4,
       decoder_2_out_5, decoder_2_out_6, decoder_2_out_7, nand_1_out, nand_2_out, not_1_out, not_2_out,
       not_3_out, not_4_out, not_5_out, not_6_out, not_7_out, not_8_out, not_9_out, not_10_out, not_11_out,
       not_12_out, not_13_out, not_14_out, not_15_out, not_16_out, not_17_out, not_18_out, not_19_out,
       not_20_out, not_21_out, not_22_out, not_23_out, not_24_out, not_25_out, not_26_out, not_27_out,
       not_28_out, not_29_out, not_30_out, not_31_out, not_32_out, not_33_out, not_34_out, not_35_out,
       not_36_out, not_37_out, not_38_out, not_39_out, not_40_out, not_41_out, not_42_out, not_43_out,
       not_44_out, not_45_out, not_46_out, not_47_out, not_48_out, not_49_out, not_50_out, not_51_out,
       not_52_out, not_53_out, not_54_out, not_55_out, not_56_out, not_57_out, not_58_out, not_59_out,
       not_60_out, not_61_out, not_62_out, not_63_out, not_64_out, not_65_out, not_66_out, not_67_out,
       not_68_out, not_69_out, not_70_out, not_71_out, not_72_out, not_73_out, not_74_out, not_75_out,
       not_76_out, not_77_out, not_78_out, not_79_out, not_80_out, not_81_out, not_82_out, not_83_out,
       not_84_out, not_85_out, not_86_out, not_87_out, not_88_out, not_89_out, not_90_out, not_91_out,
       not_92_out, not_93_out, not_94_out, not_95_out, not_96_out, not_97_out, not_98_out, not_99_out,
       not_100_out, not_101_out, not_102_out, not_103_out, not_104_out, not_105_out, not_106_out,
       not_107_out, not_108_out, not_109_out, not_110_out, not_111_out, not_112_out, not_113_out,
       not_114_out, not_115_out, not_116_out, not_117_out, not_118_out, not_119_out, not_120_out,
       not_121_out, not_122_out, not_123_out, not_124_out, not_125_out, not_126_out, not_127_out,
       not_128_out, not_129_out, not_130_out, not_131_out, not_132_out, not_133_out, not_134_out,
       not_135_out, not_136_out, not_137_out, not_138_out, not_139_out, not_140_out, not_141_out,
       not_142_out, not_143_out, not_144_out, not_145_out, not_146_out, not_147_out, not_148_out,
       not_149_out, not_150_out, not_151_out, not_152_out, not_153_out, not_154_out, not_155_out,
       not_156_out, not_157_out, not_158_out, or_9_out, xor_1_out, xor_2_out, xor_3_out, xor_4_out,
       xor_5_out, xor_6_out, xor_7_out, xor_8_out, xor_9_out, xor_10_out, xor_11_out, xor_12_out, xor_13_out,
       xor_14_out, xor_15_out, xor_16_out, xor_17_out, xor_18_out, xor_19_out, xor_20_out, xor_21_out,
       xor_22_out, xor_23_out, xor_24_out, xor_25_out, xor_26_out, xor_27_out, xor_28_out, xor_29_out,
       xor_30_out, xor_31_out, xor_32_out, xor_33_out, xor_34_out, xor_35_out, xor_36_out, xor_37_out,
       xor_38_out, xor_39_out, xor_40_out, xor_41_out, xor_42_out, xor_43_out, xor_44_out, xor_45_out,
       xor_46_out, xor_47_out, xor_48_out, xor_49_out, xor_50_out, xor_51_out, xor_52_out, xor_53_out,
       xor_54_out, xor_55_out, xor_56_out, xor_57_out, xor_58_out, xor_59_out, xor_60_out, xor_61_out,
       xor_62_out, xor_63_out, xor_64_out, xor_65_out, xor_66_out, xor_67_out, xor_68_out, xor_69_out,
       xor_70_out, xor_71_out, xor_72_out, xor_73_out, xor_74_out, xor_75_out, xor_76_out, xor_77_out,
       xor_78_out, xor_79_out, xor_80_out, xor_81_out, xor_82_out, xor_83_out, xor_84_out, xor_85_out,
       xor_86_out, xor_87_out, xor_88_out, xor_89_out, xor_90_out, xor_91_out, xor_92_out, xor_93_out,
       xor_94_out, xor_95_out, xor_96_out, xor_97_out, xor_98_out, xor_99_out, xor_100_out, xor_101_out,
       xor_102_out, xor_103_out, xor_104_out, xor_105_out, xor_106_out, xor_107_out, xor_108_out,
       xor_109_out, xor_110_out, xor_111_out, xor_112_out, xor_113_out, xor_114_out, xor_115_out;
  wire [1:0] or_4_out;
  wire [2:0] counter_1_out, d_ff_2_q, d_ff_3_q, d_ff_4_q, d_ff_5_q, d_ff_6_q, d_ff_7_q, d_ff_8_q, d_ff_9_q,
       d_ff_10_q, multiplexer_1_out, multiplexer_2_out, multiplexer_3_out, or_2_out, or_8_out;
  wire [5:0] register_2_q, register_3_q, register_4_q;
  wire [6:0] d_ff_12_nq, d_ff_13_nq, d_ff_17_nq, d_ff_18_nq, d_ff_19_nq;
  wire [6:6] d_ff_14_nq, d_ff_15_nq, d_ff_16_nq;
  wire [7:0] multiplexer_4_out, register_9_q, register_10_q, register_11_q, register_12_q, register_13_q,
       register_14_q, register_15_q, register_16_q;

  xor xor_1 (xor_1_out, d_ff_12_nq[0], Write_Key[0]);
  xor xor_2 (xor_2_out, d_ff_12_nq[1], Write_Key[1]);
  xor xor_3 (xor_3_out, d_ff_12_nq[2], Write_Key[2]);
  xor xor_4 (xor_4_out, Write_Key[3], d_ff_12_nq[3]);
  xor xor_5 (xor_5_out, d_ff_12_nq[4], Write_Key[4]);
  xor xor_6 (xor_6_out, d_ff_12_nq[5], Write_Key[5]);
  xor xor_7 (xor_7_out, 1'b0, d_ff_12_nq[6]);
  not not_1 (not_1_out, xor_1_out);
  not not_2 (not_2_out, xor_2_out);
  not not_3 (not_3_out, xor_3_out);
  not not_4 (not_4_out, xor_4_out);
  not not_5 (not_5_out, xor_5_out);
  not not_6 (not_6_out, xor_6_out);
  not not_7 (not_7_out, xor_7_out);
  xor xor_8 (xor_8_out, register_2_q[0], Write_Key[0]);
  xor xor_9 (xor_9_out, register_2_q[1], Write_Key[1]);
  xor xor_10 (xor_10_out, register_2_q[2], Write_Key[2]);
  xor xor_11 (xor_11_out, Write_Key[3], register_2_q[3]);
  xor xor_12 (xor_12_out, register_2_q[4], Write_Key[4]);
  xor xor_13 (xor_13_out, register_2_q[5], Write_Key[5]);
  xor xor_14 (xor_14_out, 1'b0, d_ff_16_nq[6]);
  xor xor_15 (xor_15_out, Write_Key[3], register_3_q[3]);
  xor xor_16 (xor_16_out, register_3_q[4], Write_Key[4]);
  not not_8 (not_8_out, xor_8_out);
  not not_9 (not_9_out, xor_9_out);
  not not_10 (not_10_out, xor_10_out);
  not not_11 (not_11_out, xor_11_out);
  not not_12 (not_12_out, xor_12_out);
  not not_13 (not_13_out, xor_13_out);
  not not_14 (not_14_out, xor_14_out);
  xor xor_17 (xor_17_out, register_3_q[0], Write_Key[0]);
  xor xor_18 (xor_18_out, register_3_q[1], Write_Key[1]);
  xor xor_19 (xor_19_out, register_3_q[2], Write_Key[2]);
  xor xor_20 (xor_20_out, register_3_q[5], Write_Key[5]);
  xor xor_21 (xor_21_out, 1'b0, d_ff_15_nq[6]);
  xor xor_22 (xor_22_out, register_4_q[0], Write_Key[0]);
  xor xor_23 (xor_23_out, register_4_q[1], Write_Key[1]);
  xor xor_24 (xor_24_out, register_4_q[2], Write_Key[2]);
  xor xor_25 (xor_25_out, Write_Key[3], register_4_q[3]);
  xor xor_26 (xor_26_out, register_4_q[4], Write_Key[4]);
  xor xor_27 (xor_27_out, register_4_q[5], Write_Key[5]);
  xor xor_28 (xor_28_out, 1'b0, d_ff_14_nq[6]);
  xor xor_29 (xor_29_out, d_ff_13_nq[0], Write_Key[0]);
  xor xor_30 (xor_30_out, d_ff_13_nq[1], Write_Key[1]);
  xor xor_31 (xor_31_out, d_ff_13_nq[2], Write_Key[2]);
  xor xor_32 (xor_32_out, Write_Key[3], d_ff_13_nq[3]);
  xor xor_33 (xor_33_out, d_ff_13_nq[4], Write_Key[4]);
  xor xor_34 (xor_34_out, d_ff_13_nq[5], Write_Key[5]);
  xor xor_35 (xor_35_out, 1'b0, d_ff_13_nq[6]);
  xor xor_36 (xor_36_out, Write_Key[3], d_ff_19_nq[3]);
  xor xor_37 (xor_37_out, d_ff_19_nq[4], Write_Key[4]);
  and and_1 (and_1_out, not_1_out, not_2_out, not_3_out, not_4_out, not_5_out, not_6_out, not_7_out);
  not not_15 (not_15_out, xor_17_out);
  not not_16 (not_16_out, xor_18_out);
  not not_17 (not_17_out, xor_19_out);
  not not_18 (not_18_out, xor_15_out);
  not not_19 (not_19_out, xor_16_out);
  not not_20 (not_20_out, xor_20_out);
  not not_21 (not_21_out, xor_21_out);
  not not_22 (not_22_out, xor_22_out);
  not not_23 (not_23_out, xor_23_out);
  not not_24 (not_24_out, xor_24_out);
  not not_25 (not_25_out, xor_25_out);
  not not_26 (not_26_out, xor_26_out);
  not not_27 (not_27_out, xor_27_out);
  not not_28 (not_28_out, xor_28_out);
  not not_29 (not_29_out, xor_29_out);
  not not_30 (not_30_out, xor_30_out);
  not not_31 (not_31_out, xor_31_out);
  not not_32 (not_32_out, xor_32_out);
  not not_33 (not_33_out, xor_33_out);
  not not_34 (not_34_out, xor_34_out);
  not not_35 (not_35_out, xor_35_out);
  xor xor_38 (xor_38_out, d_ff_19_nq[0], Write_Key[0]);
  xor xor_39 (xor_39_out, d_ff_19_nq[1], Write_Key[1]);
  xor xor_40 (xor_40_out, d_ff_19_nq[2], Write_Key[2]);
  xor xor_41 (xor_41_out, d_ff_19_nq[5], Write_Key[5]);
  xor xor_42 (xor_42_out, 1'b0, d_ff_19_nq[6]);
  xor xor_43 (xor_43_out, d_ff_18_nq[0], Write_Key[0]);
  xor xor_44 (xor_44_out, d_ff_18_nq[1], Write_Key[1]);
  xor xor_45 (xor_45_out, d_ff_18_nq[2], Write_Key[2]);
  xor xor_46 (xor_46_out, Write_Key[3], d_ff_18_nq[3]);
  xor xor_47 (xor_47_out, d_ff_18_nq[4], Write_Key[4]);
  xor xor_48 (xor_48_out, d_ff_18_nq[5], Write_Key[5]);
  xor xor_49 (xor_49_out, 1'b0, d_ff_18_nq[6]);
  xor xor_50 (xor_50_out, d_ff_17_nq[0], Write_Key[0]);
  xor xor_51 (xor_51_out, d_ff_17_nq[1], Write_Key[1]);
  xor xor_52 (xor_52_out, d_ff_17_nq[2], Write_Key[2]);
  xor xor_53 (xor_53_out, Write_Key[3], d_ff_17_nq[3]);
  xor xor_54 (xor_54_out, d_ff_17_nq[4], Write_Key[4]);
  xor xor_55 (xor_55_out, d_ff_17_nq[5], Write_Key[5]);
  xor xor_56 (xor_56_out, 1'b0, d_ff_17_nq[6]);
  and and_2 (and_2_out, not_8_out, not_9_out, not_10_out, not_11_out, not_12_out, not_13_out, not_14_out);
  and and_3 (and_3_out, not_15_out, not_16_out, not_17_out, not_18_out, not_19_out, not_20_out, not_21_out);
  not not_36 (not_36_out, xor_38_out);
  not not_37 (not_37_out, xor_39_out);
  not not_38 (not_38_out, xor_40_out);
  not not_39 (not_39_out, xor_36_out);
  not not_40 (not_40_out, xor_37_out);
  not not_41 (not_41_out, xor_41_out);
  not not_42 (not_42_out, xor_42_out);
  not not_43 (not_43_out, xor_43_out);
  not not_44 (not_44_out, xor_44_out);
  not not_45 (not_45_out, xor_45_out);
  not not_46 (not_46_out, xor_46_out);
  not not_47 (not_47_out, xor_47_out);
  not not_48 (not_48_out, xor_48_out);
  not not_49 (not_49_out, xor_49_out);
  not not_50 (not_50_out, xor_53_out);
  not not_51 (not_51_out, xor_54_out);
  and and_4 (and_4_out, not_22_out, not_23_out, not_24_out, not_25_out, not_26_out, not_27_out, not_28_out);
  and and_5 (and_5_out, not_29_out, not_30_out, not_31_out, not_32_out, not_33_out, not_34_out, not_35_out);
  and and_6 (and_6_out, not_36_out, not_37_out, not_38_out, not_39_out, not_40_out, not_41_out, not_42_out);
  not not_52 (not_52_out, xor_50_out);
  not not_53 (not_53_out, xor_51_out);
  not not_54 (not_54_out, xor_52_out);
  not not_55 (not_55_out, xor_55_out);
  not not_56 (not_56_out, xor_56_out);
  and and_7 (and_7_out, not_43_out, not_44_out, not_45_out, not_46_out, not_47_out, not_48_out, not_49_out);
  and and_8 (and_8_out, not_52_out, not_53_out, not_54_out, not_50_out, not_51_out, not_55_out, not_56_out);
  or or_1 (or_2_out[1], and_3_out, and_4_out, and_7_out, and_8_out);
  or or_2 (or_2_out[2], and_5_out, and_6_out, and_7_out, and_8_out);
  or or_3 (or_2_out[0], and_2_out, and_4_out, and_6_out, and_8_out);
  or or_4 (or_4_out[1], and_1_out, and_2_out, and_3_out, and_4_out, and_5_out, and_6_out, and_7_out, and_8_out);
  D_FF d_ff_1 (.D(or_4_out[1]), .C(clk), .Q(d_ff_1_q));  // open: nQ
  and and_9 (and_9_out, d_ff_1_q, clk);
  not not_57 (not_57_out, or_4_out[1]);
  and and_10 (and_10_out, clk, not_57_out);
  D_FF #(.Bits(3)) d_ff_2 (.D(multiplexer_3_out), .C(and_10_out), .Q(d_ff_2_q));  // open: nQ
  D_FF #(.Bits(3)) d_ff_3 (.D(d_ff_2_q), .C(and_10_out), .Q(d_ff_3_q));  // open: nQ
  D_FF #(.Bits(3)) d_ff_4 (.D(d_ff_3_q), .C(and_10_out), .Q(d_ff_4_q));  // open: nQ
  D_FF #(.Bits(3)) d_ff_5 (.D(d_ff_4_q), .C(and_10_out), .Q(d_ff_5_q));  // open: nQ
  D_FF #(.Bits(3)) d_ff_6 (.D(d_ff_5_q), .C(and_10_out), .Q(d_ff_6_q));  // open: nQ
  D_FF #(.Bits(3)) d_ff_7 (.D(d_ff_6_q), .C(and_10_out), .Q(d_ff_7_q));  // open: nQ
  D_FF #(.Bits(3)) d_ff_8 (.D(d_ff_7_q), .C(and_10_out), .Q(d_ff_8_q));  // open: nQ
  D_FF #(.Bits(3)) d_ff_9 (.D(or_2_out), .C(and_9_out), .Q(d_ff_9_q));  // open: nQ
  D_FF #(.Bits(3)) d_ff_10 (.D(d_ff_8_q), .C(and_10_out), .Q(d_ff_10_q));  // open: nQ
  xor xor_57 (xor_57_out, d_ff_9_q[0], d_ff_10_q[0]);
  xor xor_58 (xor_58_out, d_ff_9_q[1], d_ff_10_q[1]);
  xor xor_59 (xor_59_out, d_ff_9_q[2], d_ff_10_q[2]);
  not not_58 (not_58_out, xor_57_out);
  not not_59 (not_59_out, xor_58_out);
  not not_60 (not_60_out, xor_59_out);
  and and_11 (and_11_out, and_9_out, not_58_out, not_59_out, not_60_out);
  not not_61 (not_61_out, or_4_out[1]);
  and and_12 (and_12_out, not_61_out, clk);
  Counter #(.Bits(3)) counter_1 (.en(not_62_out), .C(and_12_out), .clr(and_37_out), .out(counter_1_out));  // open: ovf
  xor xor_60 (xor_60_out, d_ff_12_nq[0], Read_Key[0]);
  xor xor_61 (xor_61_out, d_ff_12_nq[1], Read_Key[1]);
  xor xor_62 (xor_62_out, d_ff_12_nq[2], Read_Key[2]);
  xor xor_63 (xor_63_out, Read_Key[3], d_ff_12_nq[3]);
  xor xor_64 (xor_64_out, d_ff_12_nq[4], Read_Key[4]);
  xor xor_65 (xor_65_out, d_ff_12_nq[5], Read_Key[5]);
  xor xor_66 (xor_66_out, 1'b0, d_ff_12_nq[6]);
  not not_62 (not_62_out, or_4_out[0]);
  not not_63 (not_63_out, xor_60_out);
  not not_64 (not_64_out, xor_61_out);
  not not_65 (not_65_out, xor_62_out);
  not not_66 (not_66_out, xor_63_out);
  not not_67 (not_67_out, xor_64_out);
  not not_68 (not_68_out, xor_65_out);
  not not_69 (not_69_out, xor_66_out);
  xor xor_67 (xor_67_out, register_2_q[0], Read_Key[0]);
  xor xor_68 (xor_68_out, register_2_q[1], Read_Key[1]);
  xor xor_69 (xor_69_out, register_2_q[2], Read_Key[2]);
  xor xor_70 (xor_70_out, Read_Key[3], register_2_q[3]);
  xor xor_71 (xor_71_out, register_2_q[4], Read_Key[4]);
  xor xor_72 (xor_72_out, register_2_q[5], Read_Key[5]);
  xor xor_73 (xor_73_out, 1'b0, d_ff_16_nq[6]);
  xor xor_74 (xor_74_out, Read_Key[3], register_3_q[3]);
  xor xor_75 (xor_75_out, register_3_q[4], Read_Key[4]);
  not not_70 (not_70_out, xor_67_out);
  not not_71 (not_71_out, xor_68_out);
  not not_72 (not_72_out, xor_69_out);
  not not_73 (not_73_out, xor_70_out);
  not not_74 (not_74_out, xor_71_out);
  not not_75 (not_75_out, xor_72_out);
  not not_76 (not_76_out, xor_73_out);
  xor xor_76 (xor_76_out, register_3_q[0], Read_Key[0]);
  xor xor_77 (xor_77_out, register_3_q[1], Read_Key[1]);
  xor xor_78 (xor_78_out, register_3_q[2], Read_Key[2]);
  xor xor_79 (xor_79_out, register_3_q[5], Read_Key[5]);
  xor xor_80 (xor_80_out, 1'b0, d_ff_15_nq[6]);
  xor xor_81 (xor_81_out, register_4_q[0], Read_Key[0]);
  xor xor_82 (xor_82_out, register_4_q[1], Read_Key[1]);
  xor xor_83 (xor_83_out, register_4_q[2], Read_Key[2]);
  xor xor_84 (xor_84_out, Read_Key[3], register_4_q[3]);
  xor xor_85 (xor_85_out, register_4_q[4], Read_Key[4]);
  xor xor_86 (xor_86_out, register_4_q[5], Read_Key[5]);
  xor xor_87 (xor_87_out, 1'b0, d_ff_14_nq[6]);
  xor xor_88 (xor_88_out, d_ff_13_nq[0], Read_Key[0]);
  xor xor_89 (xor_89_out, d_ff_13_nq[1], Read_Key[1]);
  xor xor_90 (xor_90_out, d_ff_13_nq[2], Read_Key[2]);
  xor xor_91 (xor_91_out, Read_Key[3], d_ff_13_nq[3]);
  xor xor_92 (xor_92_out, d_ff_13_nq[4], Read_Key[4]);
  xor xor_93 (xor_93_out, d_ff_13_nq[5], Read_Key[5]);
  xor xor_94 (xor_94_out, 1'b0, d_ff_13_nq[6]);
  xor xor_95 (xor_95_out, Read_Key[3], d_ff_19_nq[3]);
  xor xor_96 (xor_96_out, d_ff_19_nq[4], Read_Key[4]);
  and and_13 (and_13_out, not_63_out, not_64_out, not_65_out, not_66_out, not_67_out, not_68_out, not_69_out);
  not not_77 (not_77_out, xor_76_out);
  not not_78 (not_78_out, xor_77_out);
  not not_79 (not_79_out, xor_78_out);
  not not_80 (not_80_out, xor_74_out);
  not not_81 (not_81_out, xor_75_out);
  not not_82 (not_82_out, xor_79_out);
  not not_83 (not_83_out, xor_80_out);
  not not_84 (not_84_out, xor_81_out);
  not not_85 (not_85_out, xor_82_out);
  not not_86 (not_86_out, xor_83_out);
  not not_87 (not_87_out, xor_84_out);
  not not_88 (not_88_out, xor_85_out);
  not not_89 (not_89_out, xor_86_out);
  not not_90 (not_90_out, xor_87_out);
  not not_91 (not_91_out, xor_88_out);
  not not_92 (not_92_out, xor_89_out);
  not not_93 (not_93_out, xor_90_out);
  not not_94 (not_94_out, xor_91_out);
  not not_95 (not_95_out, xor_92_out);
  not not_96 (not_96_out, xor_93_out);
  not not_97 (not_97_out, xor_94_out);
  xor xor_97 (xor_97_out, d_ff_19_nq[0], Read_Key[0]);
  xor xor_98 (xor_98_out, d_ff_19_nq[1], Read_Key[1]);
  xor xor_99 (xor_99_out, d_ff_19_nq[2], Read_Key[2]);
  xor xor_100 (xor_100_out, d_ff_19_nq[5], Read_Key[5]);
  xor xor_101 (xor_101_out, 1'b0, d_ff_19_nq[6]);
  xor xor_102 (xor_102_out, d_ff_18_nq[0], Read_Key[0]);
  xor xor_103 (xor_103_out, d_ff_18_nq[1], Read_Key[1]);
  xor xor_104 (xor_104_out, d_ff_18_nq[2], Read_Key[2]);
  xor xor_105 (xor_105_out, Read_Key[3], d_ff_18_nq[3]);
  xor xor_106 (xor_106_out, d_ff_18_nq[4], Read_Key[4]);
  xor xor_107 (xor_107_out, d_ff_18_nq[5], Read_Key[5]);
  xor xor_108 (xor_108_out, 1'b0, d_ff_18_nq[6]);
  xor xor_109 (xor_109_out, d_ff_17_nq[0], Read_Key[0]);
  xor xor_110 (xor_110_out, d_ff_17_nq[1], Read_Key[1]);
  xor xor_111 (xor_111_out, d_ff_17_nq[2], Read_Key[2]);
  xor xor_112 (xor_112_out, Read_Key[3], d_ff_17_nq[3]);
  xor xor_113 (xor_113_out, d_ff_17_nq[4], Read_Key[4]);
  xor xor_114 (xor_114_out, d_ff_17_nq[5], Read_Key[5]);
  xor xor_115 (xor_115_out, 1'b0, d_ff_17_nq[6]);
  D_FF d_ff_11 (.D(and_37_out), .C(clk), .Q(or_4_out[0]));  // open: nQ
  and and_14 (and_14_out, not_70_out, not_71_out, not_72_out, not_73_out, not_74_out, not_75_out, not_76_out);
  and and_15 (and_15_out, not_77_out, not_78_out, not_79_out, not_80_out, not_81_out, not_82_out, not_83_out);
  not not_98 (not_98_out, xor_97_out);
  not not_99 (not_99_out, xor_98_out);
  not not_100 (not_100_out, xor_99_out);
  not not_101 (not_101_out, xor_95_out);
  not not_102 (not_102_out, xor_96_out);
  not not_103 (not_103_out, xor_100_out);
  not not_104 (not_104_out, xor_101_out);
  not not_105 (not_105_out, xor_102_out);
  not not_106 (not_106_out, xor_103_out);
  not not_107 (not_107_out, xor_104_out);
  not not_108 (not_108_out, xor_105_out);
  not not_109 (not_109_out, xor_106_out);
  not not_110 (not_110_out, xor_107_out);
  not not_111 (not_111_out, xor_108_out);
  not not_112 (not_112_out, xor_112_out);
  not not_113 (not_113_out, xor_113_out);
  and and_16 (and_16_out, not_84_out, not_85_out, not_86_out, not_87_out, not_88_out, not_89_out, not_90_out);
  and and_17 (and_17_out, not_91_out, not_92_out, not_93_out, not_94_out, not_95_out, not_96_out, not_97_out);
  not not_114 (not_114_out, xor_109_out);
  not not_115 (not_115_out, xor_110_out);
  not not_116 (not_116_out, xor_111_out);
  not not_117 (not_117_out, xor_114_out);
  not not_118 (not_118_out, xor_115_out);
  and and_18 (and_18_out, and_45_out, clk);
  and and_19 (and_19_out, and_44_out, clk);
  and and_20 (and_20_out, and_43_out, clk);
  and and_21 (and_21_out, and_42_out, clk);
  Multiplexer #(.Bits(3)) multiplexer_1 (
    .sel(clk), .in_0(d_ff_10_q), .in_1(multiplexer_1_out), .out(multiplexer_1_out));
  Multiplexer #(.Bits(3)) multiplexer_2 (
    .sel(clk), .in_0(counter_1_out), .in_1(multiplexer_2_out), .out(multiplexer_2_out));
  and and_22 (and_22_out, and_41_out, clk);
  and and_23 (and_23_out, and_40_out, clk);
  and and_24 (and_24_out, and_39_out, clk);
  and and_25 (and_25_out, and_38_out, clk);
  and and_26 (and_26_out, not_98_out, not_99_out, not_100_out, not_101_out, not_102_out, not_103_out, not_104_out);
  and and_27 (and_27_out, not_105_out, not_106_out, not_107_out, not_108_out, not_109_out, not_110_out, not_111_out);
  and and_28 (and_28_out, not_114_out, not_115_out, not_116_out, not_112_out, not_113_out, not_117_out, not_118_out);
  Multiplexer #(.Bits(3), .Selector_Bits(2)) multiplexer_3 (
    .sel(or_4_out), .in_0(multiplexer_2_out), .in_1(multiplexer_1_out), .in_2(or_2_out), .in_3(or_2_out),
    .out(multiplexer_3_out));
  Decoder #(.Selector_Bits(3)) decoder_1 (
    .sel(multiplexer_3_out), .out_0(decoder_1_out_0), .out_1(decoder_1_out_1), .out_2(decoder_1_out_2),
    .out_3(decoder_1_out_3), .out_4(decoder_1_out_4), .out_5(decoder_1_out_5), .out_6(decoder_1_out_6),
    .out_7(decoder_1_out_7));
  and and_29 (and_29_out, decoder_1_out_0, clk);
  and and_30 (and_30_out, decoder_1_out_1, clk);
  and and_31 (and_31_out, decoder_1_out_2, clk);
  and and_32 (and_32_out, decoder_1_out_3, clk);
  and and_33 (and_33_out, decoder_1_out_4, clk);
  and and_34 (and_34_out, decoder_1_out_5, clk);
  and and_35 (and_35_out, decoder_1_out_6, clk);
  and and_36 (and_36_out, decoder_1_out_7, clk);
  D_FF d_ff_12 (.D(decoder_1_out_0), .C(and_25_out), .nQ(d_ff_12_nq[6]));  // open: Q
  D_FF d_ff_13 (.D(decoder_1_out_4), .C(and_21_out), .nQ(d_ff_13_nq[6]));  // open: Q
  D_FF d_ff_14 (.D(decoder_1_out_3), .C(and_22_out), .nQ(d_ff_14_nq[6]));  // open: Q
  D_FF d_ff_15 (.D(decoder_1_out_2), .C(and_23_out), .nQ(d_ff_15_nq[6]));  // open: Q
  D_FF d_ff_16 (.D(decoder_1_out_1), .C(and_24_out), .nQ(d_ff_16_nq[6]));  // open: Q
  D_FF d_ff_17 (.D(decoder_1_out_7), .C(and_18_out), .nQ(d_ff_17_nq[6]));  // open: Q
  D_FF d_ff_18 (.D(decoder_1_out_6), .C(and_19_out), .nQ(d_ff_18_nq[6]));  // open: Q
  D_FF d_ff_19 (.D(decoder_1_out_5), .C(and_20_out), .nQ(d_ff_19_nq[6]));  // open: Q
  Register #(.Bits(6)) register_1 (.D(Write_Key), .C(and_29_out), .en(1'b1), .Q(d_ff_12_nq[5:0]));
  Register #(.Bits(6)) register_2 (.D(Write_Key), .C(and_30_out), .en(1'b1), .Q(register_2_q));
  Register #(.Bits(6)) register_3 (.D(Write_Key), .C(and_31_out), .en(1'b1), .Q(register_3_q));
  Register #(.Bits(6)) register_4 (.D(Write_Key), .C(and_32_out), .en(1'b1), .Q(register_4_q));
  Register #(.Bits(6)) register_5 (.D(Write_Key), .C(and_33_out), .en(1'b1), .Q(d_ff_13_nq[5:0]));
  Register #(.Bits(6)) register_6 (.D(Write_Key), .C(and_34_out), .en(1'b1), .Q(d_ff_19_nq[5:0]));
  Register #(.Bits(6)) register_7 (.D(Write_Key), .C(and_35_out), .en(1'b1), .Q(d_ff_18_nq[5:0]));
  Register #(.Bits(6)) register_8 (.D(Write_Key), .C(and_36_out), .en(1'b1), .Q(d_ff_17_nq[5:0]));
  // Or or_5 has open pins: In_1=and_38_out, In_2=and_37_out, out=open
  not not_119 (not_119_out, d_ff_12_nq[6]);
  not not_120 (not_120_out, d_ff_16_nq[6]);
  not not_121 (not_121_out, d_ff_15_nq[6]);
  not not_122 (not_122_out, d_ff_14_nq[6]);
  not not_123 (not_123_out, d_ff_13_nq[6]);
  not not_124 (not_124_out, d_ff_19_nq[6]);
  or or_6 (or_8_out[1], and_15_out, and_16_out, and_27_out, and_28_out);
  or or_7 (or_8_out[2], and_17_out, and_26_out, and_27_out, and_28_out);
  not not_125 (not_125_out, d_ff_18_nq[6]);
  not not_126 (not_126_out, d_ff_17_nq[6]);
  and and_37 (and_37_out, not_126_out, not_125_out, not_124_out, not_123_out, not_122_out, not_121_out, not_120_out, not_119_out);
  or or_8 (or_8_out[0], and_14_out, and_16_out, and_26_out, and_28_out);
  or or_9 (or_9_out, d_ff_17_nq[6], d_ff_18_nq[6], d_ff_19_nq[6], d_ff_13_nq[6], d_ff_14_nq[6], d_ff_15_nq[6], d_ff_16_nq[6], d_ff_12_nq[6]);
  and and_38 (and_38_out, d_ff_17_nq[6], d_ff_18_nq[6], d_ff_19_nq[6], d_ff_13_nq[6], d_ff_14_nq[6], d_ff_15_nq[6], d_ff_16_nq[6], d_ff_12_nq[6]);
  not not_127 (not_127_out, d_ff_12_nq[6]);
  not not_128 (not_128_out, d_ff_12_nq[6]);
  and and_39 (and_39_out, d_ff_17_nq[6], d_ff_18_nq[6], d_ff_19_nq[6], d_ff_13_nq[6], d_ff_14_nq[6], d_ff_15_nq[6], d_ff_16_nq[6], not_127_out);
  not not_129 (not_129_out, d_ff_16_nq[6]);
  and and_40 (and_40_out, d_ff_17_nq[6], d_ff_18_nq[6], d_ff_19_nq[6], d_ff_13_nq[6], d_ff_14_nq[6], d_ff_15_nq[6], not_129_out, not_128_out);
  not not_130 (not_130_out, d_ff_12_nq[6]);
  not not_131 (not_131_out, d_ff_16_nq[6]);
  not not_132 (not_132_out, d_ff_15_nq[6]);
  and and_41 (and_41_out, d_ff_17_nq[6], d_ff_18_nq[6], d_ff_19_nq[6], d_ff_13_nq[6], d_ff_14_nq[6], not_132_out, not_131_out, not_130_out);
  not not_133 (not_133_out, d_ff_12_nq[6]);
  not not_134 (not_134_out, d_ff_16_nq[6]);
  not not_135 (not_135_out, d_ff_15_nq[6]);
  not not_136 (not_136_out, d_ff_14_nq[6]);
  not not_137 (not_137_out, d_ff_12_nq[6]);
  not not_138 (not_138_out, d_ff_16_nq[6]);
  and and_42 (and_42_out, d_ff_17_nq[6], d_ff_18_nq[6], d_ff_19_nq[6], d_ff_13_nq[6], not_136_out, not_135_out, not_134_out, not_133_out);
  not not_139 (not_139_out, d_ff_15_nq[6]);
  not not_140 (not_140_out, d_ff_14_nq[6]);
  not not_141 (not_141_out, d_ff_13_nq[6]);
  and and_43 (and_43_out, d_ff_17_nq[6], d_ff_18_nq[6], d_ff_19_nq[6], not_141_out, not_140_out, not_139_out, not_138_out, not_137_out);
  not not_142 (not_142_out, d_ff_12_nq[6]);
  not not_143 (not_143_out, d_ff_16_nq[6]);
  not not_144 (not_144_out, d_ff_15_nq[6]);
  not not_145 (not_145_out, d_ff_14_nq[6]);
  not not_146 (not_146_out, d_ff_13_nq[6]);
  not not_147 (not_147_out, d_ff_19_nq[6]);
  and and_44 (and_44_out, d_ff_17_nq[6], d_ff_18_nq[6], not_147_out, not_146_out, not_145_out, not_144_out, not_143_out, not_142_out);
  not not_148 (not_148_out, d_ff_12_nq[6]);
  not not_149 (not_149_out, d_ff_16_nq[6]);
  not not_150 (not_150_out, d_ff_15_nq[6]);
  not not_151 (not_151_out, d_ff_14_nq[6]);
  Decoder #(.Selector_Bits(3)) decoder_2 (
    .sel(multiplexer_3_out), .out_0(decoder_2_out_0), .out_1(decoder_2_out_1), .out_2(decoder_2_out_2),
    .out_3(decoder_2_out_3), .out_4(decoder_2_out_4), .out_5(decoder_2_out_5), .out_6(decoder_2_out_6),
    .out_7(decoder_2_out_7));
  not not_152 (not_152_out, d_ff_13_nq[6]);
  not not_153 (not_153_out, d_ff_19_nq[6]);
  not not_154 (not_154_out, d_ff_18_nq[6]);
  and and_45 (and_45_out, d_ff_17_nq[6], not_154_out, not_153_out, not_152_out, not_151_out, not_150_out, not_149_out, not_148_out);
  and and_46 (and_46_out, decoder_2_out_0, clk);
  and and_47 (and_47_out, decoder_2_out_1, clk);
  and and_48 (and_48_out, decoder_2_out_2, clk);
  and and_49 (and_49_out, decoder_2_out_3, clk);
  and and_50 (and_50_out, decoder_2_out_4, clk);
  and and_51 (and_51_out, decoder_2_out_5, clk);
  and and_52 (and_52_out, decoder_2_out_6, clk);
  and and_53 (and_53_out, decoder_2_out_7, clk);
  nand nand_1 (nand_1_out, d_ff_17_nq[6], d_ff_18_nq[6], d_ff_19_nq[6], d_ff_13_nq[6], d_ff_14_nq[6], d_ff_15_nq[6], d_ff_16_nq[6], d_ff_12_nq[6]);
  Register #(.Bits(8)) register_9 (.D(Write_Value), .C(and_46_out), .en(1'b1), .Q(register_9_q));
  Register #(.Bits(8)) register_10 (.D(Write_Value), .C(and_47_out), .en(1'b1), .Q(register_10_q));
  Register #(.Bits(8)) register_11 (.D(Write_Value), .C(and_48_out), .en(1'b1), .Q(register_11_q));
  Register #(.Bits(8)) register_12 (.D(Write_Value), .C(and_49_out), .en(1'b1), .Q(register_12_q));
  Register #(.Bits(8)) register_13 (.D(Write_Value), .C(and_50_out), .en(1'b1), .Q(register_13_q));
  Register #(.Bits(8)) register_14 (.D(Write_Value), .C(and_51_out), .en(1'b1), .Q(register_14_q));
  Register #(.Bits(8)) register_15 (.D(Write_Value), .C(and_52_out), .en(1'b1), .Q(register_15_q));
  Register #(.Bits(8)) register_16 (.D(Write_Value), .C(and_53_out), .en(1'b1), .Q(register_16_q));
  not not_155 (not_155_out, or_8_out[0]);
  and and_54 (and_54_out, not_155_out, not_156_out, not_157_out);
  not not_156 (not_156_out, or_8_out[1]);
  not not_157 (not_157_out, or_8_out[2]);
  assign Read_Value = nand_2_out ? multiplexer_4_out : 8'bz;  // Driver driver_1
  Multiplexer #(.Selector_Bits(3), .Bits(8)) multiplexer_4 (
    .sel(or_8_out), .in_0(register_9_q), .in_1(register_10_q), .in_2(register_11_q), .in_3(register_12_q),
    .in_4(register_13_q), .in_5(register_14_q), .in_6(register_15_q), .in_7(register_16_q),
    .out(multiplexer_4_out));
  nand nand_2 (nand_2_out, and_54_out, not_158_out);
  not not_158 (not_158_out, and_13_out);
endmodule
