// Digital circuit testing circuit.dig as structural Verilog
module testing_circuit (
  input  clk,
  input  [31:0] Rd_Val,
  input  [2:0] Rd,
  input  [2:0] Rn,
  input  [2:0] Rm,
  input  [31:0] operand_0,
  input  [31:0] operand_1,
  input  [3:0] operation,
  input  id_cc,
  input  [31:0] operand,
  output [31:0] Rm_Val,
  output [31:0] Rn_Val,
  output [31:0] result,
  output Z,
  output N,
  output P
);

  part1_circuit part1_circuit_1 (
    .Rd_val(Rd_Val), .clk(clk), .Rd(Rd), .Rn(Rn), .Rm(Rm), .Rm_Val(Rm_Val), .Rn_Val(Rn_Val));
  part2_circuit part2_circuit_1 (.operand_0(operand_0), .operand_1(operand_1), .operation(operation), .result(result));
  part3_circuit part3_circuit_1 (.Id_cc(id_cc), .operand(operand), .Z(Z), .N(N), .P(P));
endmodule
