// Digital circuit Register File circuit.dig as structural Verilog
module Register_File_circuit (
  input  [31:0] Rd_val,
  input  clk,
  input  [2:0] Rd,
  input  [2:0] Rn,
  input  [2:0] Rm,
  output [31:0] Rm_Val,
  output [31:0] Rn_Val
);

  wire and_1_out, and_2_out, and_3_out, and_4_out, and_5_out, and_6_out, and_7_out, and_8_out,
       decoder_1_out_0, decoder_1_out_1, decoder_1_out_2, decoder_1_out_3, decoder_1_out_4, decoder_1_out_5,
       decoder_1_out_6, decoder_1_out_7;
  wire [31:0] register_1_q, register_2_q, register_3_q, register_4_q, register_5_q, register_6_q,
       register_7_q, register_8_q;

  Decoder #(.Selector_Bits(3)) decoder_1 (
    .sel(Rd), .out_0(decoder_1_out_0), .out_1(decoder_1_out_1), .out_2(decoder_1_out_2),
    .out_3(decoder_1_out_3), .out_4(decoder_1_out_4), .out_5(decoder_1_out_5), .out_6(decoder_1_out_6),
    .out_7(decoder_1_out_7));
  and and_1 (and_1_out, decoder_1_out_0, clk);
  and and_2 (and_2_out, decoder_1_out_1, clk);
  and and_3 (and_3_out, decoder_1_out_2, clk);
  and and_4 (and_4_out, decoder_1_out_3, clk);
  and and_5 (and_5_out, decoder_1_out_4, clk);
  and and_6 (and_6_out, decoder_1_out_5, clk);
  and and_7 (and_7_out, decoder_1_out_6, clk);
  and and_8 (and_8_out, decoder_1_out_7, clk);
  Register #(.Bits(32)) register_1 (.D(Rd_val), .C(and_1_out), .en(1'b1), .Q(register_1_q));
  Register #(.Bits(32)) register_2 (.D(Rd_val), .C(and_2_out), .en(1'b1), .Q(register_2_q));
  Register #(.Bits(32)) register_3 (.D(Rd_val), .C(and_3_out), .en(1'b1), .Q(register_3_q));
  Register #(.Bits(32)) register_4 (.D(Rd_val), .C(and_4_out), .en(1'b1), .Q(register_4_q));
  Register #(.Bits(32)) register_5 (.D(Rd_val), .C(and_5_out), .en(1'b1), .Q(register_5_q));
  Register #(.Bits(32)) register_6 (.D(Rd_val), .C(and_6_out), .en(1'b1), .Q(register_6_q));
  Register #(.Bits(32)) register_7 (.D(Rd_val), .C(and_7_out), .en(1'b1), .Q(register_7_q));
  Register #(.Bits(32)) register_8 (.D(Rd_val), .C(and_8_out), .en(1'b1), .Q(register_8_q));
  Multiplexer #(.Selector_Bits(3), .Bits(32)) multiplexer_1 (
    .sel(Rn), .in_0(register_1_q), .in_1(register_2_q), .in_2(register_3_q), .in_3(register_4_q),
    .in_4(register_5_q), .in_5(register_6_q), .in_6(register_7_q), .in_7(register_8_q), .out(Rn_Val));
  Multiplexer #(.Selector_Bits(3), .Bits(32)) multiplexer_2 (
    .sel(Rm), .in_0(register_1_q), .in_1(register_2_q), .in_2(register_3_q), .in_3(register_4_q),
    .in_4(register_5_q), .in_5(register_6_q), .in_6(register_7_q), .in_7(register_8_q), .out(Rm_Val));
endmodule
