// Digital circuit hw5-part2-circuit.dig as structural Verilog
module hw5_part2_circuit (
  input  [31:0] Instruction,
  input  clk
);

  wire [31:0] ALU_p1, multiplexer_1_out, Register_File_rm_val, Register_File_rn_val;

  Multiplexer #(.Bits(32)) multiplexer_1 (
    .sel(Instruction[25]), .in_0(Register_File_rm_val), .in_1({{20{1'b0}}, Instruction[11:0]}),
    .out(multiplexer_1_out));
  Register_File_circuit Register_File (
    .Rd_val(ALU_p1), .clk(clk), .Rd(Instruction[14:12]), .Rn(Instruction[18:16]), .Rm(Instruction[2:0]),
    .Rm_Val(Register_File_rm_val), .Rn_Val(Register_File_rn_val));
  // ALU_circuit ALU: pin names not known; wires that end beside it: ALU_p1, Instruction[24:21], multiplexer_1_out, Register_File_rn_val
endmodule
