// Digital circuit RF.dig as structural Verilog
module RF (
  input  [2:0] Rn,
  input  [2:0] Rm,
  input  [2:0] Rd,
  input  [31:0] Rd_val,
  input  clk,
  output [31:0] Rn_val,
  output [31:0] Rm_val
);

  wire decoder_1_out_0, decoder_1_out_1, decoder_1_out_2, decoder_1_out_3, decoder_1_out_4, decoder_1_out_5,
       decoder_1_out_6, decoder_1_out_7;
  wire [31:0] r0_q, r1_q, r2_q, r3_q, r4_q, r5_q, r6_q, r7_q;

  Decoder #(.Selector_Bits(3)) decoder_1 (
    .sel(Rd), .out_0(decoder_1_out_0), .out_1(decoder_1_out_1), .out_2(decoder_1_out_2),
    .out_3(decoder_1_out_3), .out_4(decoder_1_out_4), .out_5(decoder_1_out_5), .out_6(decoder_1_out_6),
    .out_7(decoder_1_out_7));
  Register #(.Bits(32)) r0 (.D(Rd_val), .C(clk), .en(decoder_1_out_0), .Q(r0_q));
  Register #(.Bits(32)) r1 (.D(Rd_val), .C(clk), .en(decoder_1_out_1), .Q(r1_q));
  Register #(.Bits(32)) r2 (.D(Rd_val), .C(clk), .en(decoder_1_out_2), .Q(r2_q));
  Register #(.Bits(32)) r3 (.D(Rd_val), .C(clk), .en(decoder_1_out_3), .Q(r3_q));
  Register #(.Bits(32)) r4 (.D(Rd_val), .C(clk), .en(decoder_1_out_4), .Q(r4_q));
  Register #(.Bits(32)) r5 (.D(Rd_val), .C(clk), .en(decoder_1_out_5), .Q(r5_q));
  Register #(.Bits(32)) r6 (.D(Rd_val), .C(clk), .en(decoder_1_out_6), .Q(r6_q));
  Register #(.Bits(32)) r7 (.D(Rd_val), .C(clk), .en(decoder_1_out_7), .Q(r7_q));
  Multiplexer #(.Selector_Bits(3), .Bits(32)) multiplexer_1 (
    .sel(Rn), .in_0(r0_q), .in_1(r1_q), .in_2(r2_q), .in_3(r3_q), .in_4(r4_q), .in_5(r5_q), .in_6(r6_q),
    .in_7(r7_q), .out(Rn_val));
  Multiplexer #(.Selector_Bits(3), .Bits(32)) multiplexer_2 (
    .sel(Rm), .in_0(r0_q), .in_1(r1_q), .in_2(r2_q), .in_3(r3_q), .in_4(r4_q), .in_5(r5_q), .in_6(r6_q),
    .in_7(r7_q), .out(Rm_val));
endmodule
