// Digital circuit hw6 circuit.dig as structural Verilog
module hw6_circuit (
  input  clock
);

  wire and_1_out, and_2_out, and_3_out, and_4_out, and_5_out, and_6_out, and_7_out, and_8_out, is_imm,
       is_logical, multiplexer_1_out, not_1_out, not_2_out, not_3_out, not_4_out, not_5_out, not_6_out,
       not_7_out, not_8_out, not_9_out, not_10_out, not_11_out, not_12_out, or_1_out, or_2_out, or_3_out,
       part3_circuit_1_n, part3_circuit_1_p, part3_circuit_1_z;
  wire [2:0] demultiplexer_3_out_0, demultiplexer_3_out_0_3, multiplexer_2_out, multiplexer_3_out,
       multiplexer_4_out, Rd, Rn;
  wire [3:0] alu_op, demultiplexer_1_out_1_3, demultiplexer_3_out_1_3;
  wire [3:3] demultiplexer_3_out_0_4;
  wire [7:0] add_1_s, counterpreset_1_out;
  wire [11:0] demultiplexer_3_out_1, imm12;
  wire [13:0] demultiplexer_1_out_1;
  wire [27:14] demultiplexer_1_out_1_2;
  wire [31:0] add_2_s, alu_1_res, bitextender_1_out, demultiplexer_1_out_0, demultiplexer_2_out_1,
       demultiplexer_4_out_0, demultiplexer_4_out_1, demultiplexer_5_out_0, demultiplexer_5_out_1, imm,
       mul_1_mul, multiplexer_6_out, multiplexer_7_out, rf_1_rm_val, rf_1_rn_val, rom_1_d, sub_1_s,
       zero_ext_1_out;
  wire [31:3] demultiplexer_3_out_0_2;
  wire [31:12] demultiplexer_3_out_1_2;
  wire [31:15] demultiplexer_2_out_0;
  wire [63:32] mul_1_mul_2;

  and and_1 (and_1_out, and_2_out, multiplexer_1_out);
  CounterPreset #(.Bits(8)) counterpreset_1 (
    .en(1'b1), .C(clock), .dir(1'b0), .in(add_2_s[7:0]), .ld(and_1_out), .clr(1'b0), .out(counterpreset_1_out));  // open: ovf
  ROM #(.AddrBits(8), .Bits(32)) rom_1 (.A(counterpreset_1_out), .sel(1'b1), .D(rom_1_d));
  not not_1 (not_1_out, rom_1_d[26]);
  not not_2 (not_2_out, rom_1_d[24]);
  and and_2 (and_2_out, not_2_out, rom_1_d[25], not_1_out, rom_1_d[27]);
  not not_3 (not_3_out, rom_1_d[27]);
  not not_4 (not_4_out, rom_1_d[26]);
  not not_5 (not_5_out, rom_1_d[25]);
  not not_6 (not_6_out, rom_1_d[23]);
  not not_7 (not_7_out, rom_1_d[27]);
  not not_8 (not_8_out, rom_1_d[21]);
  and and_3 (and_3_out, rom_1_d[20], not_8_out, rom_1_d[22], not_6_out, rom_1_d[24], not_5_out, not_4_out, not_3_out);
  not not_9 (not_9_out, rom_1_d[26]);
  not not_10 (not_10_out, rom_1_d[23]);
  not not_11 (not_11_out, rom_1_d[21]);
  and and_4 (and_4_out, rom_1_d[20], not_11_out, rom_1_d[22], not_10_out, rom_1_d[24], rom_1_d[25], not_9_out, not_7_out);
  or or_1 (or_1_out, and_4_out, and_3_out);
  Add #(.Bits(8)) add_1 (.a(8'h4), .b(counterpreset_1_out), .c_i(1'b0), .s(add_1_s));  // open: c_o
  Demultiplexer #(.Bits(32)) demultiplexer_1 (
    .sel(and_2_out), .in(rom_1_d), .out_0(demultiplexer_1_out_0),
    .out_1({demultiplexer_1_out_1_3, demultiplexer_1_out_1_2, demultiplexer_1_out_1}));
  Demultiplexer #(.Bits(32)) demultiplexer_2 (
    .sel(or_1_out), .in(demultiplexer_1_out_0),
    .out_0({demultiplexer_2_out_0[31:26], is_imm, alu_op, demultiplexer_2_out_0[20:19], Rn, demultiplexer_2_out_0[15], Rd, imm12}),
    .out_1(demultiplexer_2_out_1));
  Demultiplexer #(.Bits(32)) demultiplexer_3 (
    .sel(and_4_out), .in(demultiplexer_2_out_1),
    .out_0({demultiplexer_3_out_0_2[31:20], demultiplexer_3_out_0_4[3], demultiplexer_3_out_0_3, demultiplexer_3_out_0_2[15:3], demultiplexer_3_out_0}),
    .out_1({demultiplexer_3_out_1_2[31:20], demultiplexer_3_out_1_3, demultiplexer_3_out_1_2[15:12], demultiplexer_3_out_1}));
  Multiplexer #(.Selector_Bits(4)) multiplexer_1 (
    .sel(demultiplexer_1_out_1_3), .in_0(part3_circuit_1_z), .in_1(not_12_out), .in_2(1'b0), .in_3(1'b0),
    .in_4(1'b0), .in_5(1'b0), .in_6(1'b0), .in_7(1'b0), .in_8(1'b0), .in_9(1'b0), .in_10(or_2_out),
    .in_11(part3_circuit_1_n), .in_12(part3_circuit_1_p), .in_13(or_3_out), .in_14(1'b1), .in_15(1'b0),
    .out(multiplexer_1_out));
  Mul #(.Bits(32)) mul_1 (.a({{18{1'b0}}, demultiplexer_1_out_1}), .b(32'h4), .mul({mul_1_mul_2, mul_1_mul}));
  not not_12 (not_12_out, part3_circuit_1_z);
  Multiplexer #(.Bits(3)) multiplexer_2 (
    .sel(and_4_out), .in_0(demultiplexer_3_out_0_3), .in_1(demultiplexer_3_out_1_3[2:0]),
    .out(multiplexer_2_out));
  Add #(.Bits(32)) add_2 (.a(mul_1_mul), .b({{24{1'b0}}, add_1_s}), .c_i(1'b0), .s(add_2_s));  // open: c_o
  or or_2 (or_2_out, part3_circuit_1_z, part3_circuit_1_p);
  or or_3 (or_3_out, part3_circuit_1_n, part3_circuit_1_z);
  and and_5 (and_5_out, ~alu_op[0], ~alu_op[1], ~alu_op[2], ~alu_op[3]);  // And
  and and_6 (and_6_out, alu_op[0], ~alu_op[1], ~alu_op[2], ~alu_op[3]);  // And
  and and_7 (and_7_out, ~alu_op[0], ~alu_op[1], alu_op[2], alu_op[3]);  // And
  Multiplexer #(.Bits(3)) multiplexer_3 (.sel(or_1_out), .in_0(Rn), .in_1(multiplexer_2_out), .out(multiplexer_3_out));
  Multiplexer #(.Bits(3)) multiplexer_4 (
    .sel(and_3_out), .in_0(imm12[2:0]), .in_1(demultiplexer_3_out_0), .out(multiplexer_4_out));
  or or_4 (is_logical, and_5_out, and_6_out, and_7_out);
  part3_circuit part3_circuit_1 (
    .Id_cc(and_8_out), .operand(sub_1_s), .Z(part3_circuit_1_z), .N(part3_circuit_1_n), .P(part3_circuit_1_p));
  and and_8 (and_8_out, or_1_out, clock);
  RF rf_1 (
    .Rn(multiplexer_3_out), .Rm(multiplexer_4_out), .Rd(Rd), .Rd_val(alu_1_res), .clk(clock),
    .Rn_val(rf_1_rn_val), .Rm_val(rf_1_rm_val));
  BitExtender #(.inputBits(12), .outputBits(32)) bitextender_1 (.in(imm12), .out(bitextender_1_out));
  zero_ext zero_ext_1 (.in(imm12), .out(zero_ext_1_out));
  Multiplexer #(.Bits(32)) multiplexer_5 (.sel(is_logical), .in_0(bitextender_1_out), .in_1(zero_ext_1_out), .out(imm));
  Sub #(.Bits(32)) sub_1 (.a(demultiplexer_4_out_1), .b(multiplexer_6_out), .c_i(1'b0), .s(sub_1_s));  // open: c_o
  Demultiplexer #(.Bits(32)) demultiplexer_4 (
    .sel(or_1_out), .in(rf_1_rn_val), .out_0(demultiplexer_4_out_0), .out_1(demultiplexer_4_out_1));
  Demultiplexer #(.Bits(32)) demultiplexer_5 (
    .sel(or_1_out), .in(rf_1_rm_val), .out_0(demultiplexer_5_out_0), .out_1(demultiplexer_5_out_1));
  Multiplexer #(.Bits(32)) multiplexer_6 (
    .sel(and_4_out), .in_0(demultiplexer_5_out_1), .in_1({{20{1'b0}}, demultiplexer_3_out_1}),
    .out(multiplexer_6_out));
  Multiplexer #(.Bits(32)) multiplexer_7 (
    .sel(is_imm), .in_0(demultiplexer_5_out_0), .in_1(imm), .out(multiplexer_7_out));
  ALU alu_1 (.op0(demultiplexer_4_out_0), .op1(multiplexer_7_out), .op(alu_op), .res(alu_1_res));

  // Other names for the same wires on the sheet: Rm[2:0] = imm12[2:0]
endmodule
