// Digital circuit part3 circuit.dig as structural Verilog
module part3_circuit (
  input  Id_cc,
  input  [31:0] operand,
  output Z,
  output N,
  output P
);

  wire decoder_1_out_2, decoder_1_out_3, not_1_out, not_2_out, not_3_out, not_4_out, not_5_out, not_6_out,
       not_7_out, not_8_out, not_9_out, not_10_out, not_11_out, not_12_out, not_13_out, not_14_out,
       not_15_out, not_16_out, not_17_out, not_18_out, not_19_out, not_20_out, not_21_out, not_22_out,
       not_23_out, not_24_out, not_25_out, not_26_out, not_27_out, not_28_out, not_29_out, not_30_out,
       not_31_out;
  wire [1:0] add_1_s, d_ff_1_q_2;
  wire [30:0] d_ff_1_q;

  D_FF #(.Bits(32)) d_ff_1 (.D(operand), .C(Id_cc), .Q({d_ff_1_q_2[0], d_ff_1_q}));  // open: nQ
  not not_1 (not_1_out, d_ff_1_q[0]);
  not not_2 (not_2_out, d_ff_1_q[1]);
  not not_3 (not_3_out, d_ff_1_q[2]);
  not not_4 (not_4_out, d_ff_1_q[3]);
  not not_5 (not_5_out, d_ff_1_q[4]);
  not not_6 (not_6_out, d_ff_1_q[5]);
  not not_7 (not_7_out, d_ff_1_q[6]);
  not not_8 (not_8_out, d_ff_1_q[7]);
  not not_9 (not_9_out, d_ff_1_q[8]);
  not not_10 (not_10_out, d_ff_1_q[9]);
  not not_11 (not_11_out, d_ff_1_q[10]);
  not not_12 (not_12_out, d_ff_1_q[11]);
  not not_13 (not_13_out, d_ff_1_q[12]);
  not not_14 (not_14_out, d_ff_1_q[13]);
  not not_15 (not_15_out, d_ff_1_q[14]);
  not not_16 (not_16_out, d_ff_1_q[15]);
  not not_17 (not_17_out, d_ff_1_q[16]);
  not not_18 (not_18_out, d_ff_1_q[17]);
  not not_19 (not_19_out, d_ff_1_q[18]);
  not not_20 (not_20_out, d_ff_1_q[19]);
  not not_21 (not_21_out, d_ff_1_q[20]);
  not not_22 (not_22_out, d_ff_1_q[21]);
  not not_23 (not_23_out, d_ff_1_q[22]);
  not not_24 (not_24_out, d_ff_1_q[23]);
  not not_25 (not_25_out, d_ff_1_q[24]);
  not not_26 (not_26_out, d_ff_1_q[25]);
  not not_27 (not_27_out, d_ff_1_q[26]);
  not not_28 (not_28_out, d_ff_1_q[27]);
  not not_29 (not_29_out, d_ff_1_q[28]);
  not not_30 (not_30_out, d_ff_1_q[29]);
  not not_31 (not_31_out, d_ff_1_q[30]);
  and and_1 (d_ff_1_q_2[1], not_1_out, not_2_out, not_3_out, not_4_out, not_5_out, not_6_out, not_7_out, not_8_out, not_9_out, not_10_out, not_11_out, not_12_out, not_13_out, not_14_out, not_15_out, not_16_out, not_17_out, not_18_out, not_19_out, not_20_out, not_21_out, not_22_out, not_23_out, not_24_out, not_25_out, not_26_out, not_27_out, not_28_out, not_29_out, not_30_out, not_31_out);
  Add #(.Bits(2)) add_1 (.a(d_ff_1_q_2), .b({1'b0, d_ff_1_q_2[1]}), .c_i(1'b0), .s(add_1_s));  // open: c_o
  or or_1 (Z, decoder_1_out_2, decoder_1_out_3);
  Decoder #(.Selector_Bits(2)) decoder_1 (
    .sel(add_1_s), .out_0(P), .out_1(N), .out_2(decoder_1_out_2), .out_3(decoder_1_out_3));
endmodule
