// Digital circuit ALU.dig as structural Verilog
module ALU (
  input  [31:0] op0,
  input  [31:0] op1,
  input  [3:0] op,
  output [31:0] res
);

  wire [31:0] add_1_s, and_1_out, not_1_out, or_1_out, sub_1_s, sub_2_s, xor_1_out;

  assign and_1_out = op1 & op0;  // And and_1, 32 bits wide
  assign xor_1_out = op1 ^ op0;  // XOr xor_1, 32 bits wide
  Sub #(.Bits(32)) sub_1 (.a(op0), .b(op1), .c_i(1'b0), .s(sub_1_s));  // open: c_o
  Sub #(.Bits(32)) sub_2 (.a(op1), .b(op0), .c_i(1'b0), .s(sub_2_s));  // open: c_o
  Add #(.Bits(32)) add_1 (.a(op1), .b(op0), .c_i(1'b0), .s(add_1_s));  // open: c_o
  assign or_1_out = op1 | op0;  // Or or_1, 32 bits wide
  assign not_1_out = ~op1;  // Not not_1, 32 bits wide
  Multiplexer #(.Selector_Bits(4), .Bits(32)) multiplexer_1 (
    .sel(op), .in_0(and_1_out), .in_1(xor_1_out), .in_2(sub_1_s), .in_3(sub_2_s), .in_4(add_1_s),
    .in_5({32{1'b0}}), .in_6({32{1'b0}}), .in_7({32{1'b0}}), .in_8({32{1'b0}}), .in_9({32{1'b0}}),
    .in_10({32{1'b0}}), .in_11({32{1'b0}}), .in_12(or_1_out), .in_13(op1), .in_14({32{1'b0}}),
    .in_15(not_1_out), .out(res));
endmodule
