// Digital circuit hw5-processor.dig as structural Verilog
module hw5_processor (
  input  [31:0] Instruction,
  input  clk
);

  wire [31:0] ALU_p2, ALU_p3, Register_File_rm_val, Register_File_rn_val;

  Register_File_circuit Register_File (
    .Rd_val(ALU_p3), .clk(clk), .Rd(Instruction[14:12]), .Rn(Instruction[18:16]), .Rm(Instruction[2:0]),
    .Rm_Val(Register_File_rm_val), .Rn_Val(Register_File_rn_val));
  // ALU_circuit ALU: pin names not known; wires that end beside it: Instruction[24:21], ALU_p2, ALU_p3, Register_File_rn_val
  Multiplexer #(.Bits(32)) multiplexer_1 (
    .sel(Instruction[25]), .in_0(Register_File_rm_val), .in_1({{20{1'b0}}, Instruction[11:0]}), .out(ALU_p2));
endmodule
